// Logisim project CSIS2083.CPU.circ as structural Verilog: 5 circuits, main circuit main
module main (
  input  WE,
  input  OE,
  input  Internal_OE,
  input  WE_2,
  input  OE_2,
  input  WE_3,
  input  OE_3,
  input  WE_4,
  input  WE_5,
  input  OE_4,
  input  OE_5,
  input  WE_6,
  output [3:0] MAR_Content,
  output [7:0] IR_Content,
  output [7:0] MBR_Content,
  output [7:0] Reg_A_Content,
  output [7:0] out_17,
  output [7:0] ALU_Result,
  output [7:0] Reg_B_Content
);

  wire [3:0] bitselector_1_out, mar_1_dout;
  wire [7:0] alu_1_dout, register_1_dout;

  Clock Clock (.out(OE_4));
  Register register_1 (
    .clock(OE_4), .WE(WE_2), .Din(alu_1_dout), .OE(OE_2), .Dout(register_1_dout), .Stored_data(IR_Content));
  Register register_2 (.clock(OE_4), .WE(WE_4), .Din(alu_1_dout), .Stored_data(Reg_A_Content));  // open: OE, Dout
  ALU alu_1 (
    .Reg_A(Reg_A_Content), .Reg_B(Reg_B_Content), .OE(OE_5), .Dout(alu_1_dout), .ALU_Result(ALU_Result));  // open: Carry_out
  Register register_3 (.clock(OE_4), .WE(WE_6), .Din(alu_1_dout), .Stored_data(Reg_B_Content));  // open: OE, Dout
  BitSelector #(.group(4)) bitselector_1 (.in(register_1_dout), .out(bitselector_1_out), .sel(1'b0));
  LED D7 (.in(alu_1_dout[7]));
  LED D6 (.in(alu_1_dout[6]));
  LED D5 (.in(alu_1_dout[5]));
  LED D2 (.in(alu_1_dout[2]));
  LED D4 (.in(alu_1_dout[4]));
  LED D3 (.in(alu_1_dout[3]));
  LED D0 (.in(alu_1_dout[0]));
  LED D1 (.in(alu_1_dout[1]));
  MAR mar_1 (.clock(OE_4), .WE(WE), .Din(bitselector_1_out), .OE(OE), .Dout(mar_1_dout), .Stored_data(MAR_Content));
  assign alu_1_dout = Internal_OE ? MBR_Content : 8'bz;  // Controlled_Buffer controlled_buffer_1
  Register register_4 (
    .clock(OE_4), .WE(WE_3), .Din(alu_1_dout), .OE(OE_3), .Dout(alu_1_dout), .Stored_data(MBR_Content));
  Register register_5 (.clock(OE_4), .WE(OE_4), .Din(alu_1_dout), .OE(OE_4), .Dout(alu_1_dout), .Stored_data(out_17));
  LED D7_2 (.in(alu_1_dout[7]));
  LED D6_2 (.in(alu_1_dout[6]));
  LED D5_2 (.in(alu_1_dout[5]));
  LED D2_2 (.in(alu_1_dout[2]));
  LED D4_2 (.in(alu_1_dout[4]));
  LED D3_2 (.in(alu_1_dout[3]));
  LED D1_2 (.in(alu_1_dout[1]));
  LED D0_2 (.in(alu_1_dout[0]));

  assign WE_5 = OE_4;

  // Notes on the sheet:
  //   Instruction Register
  //   Register A
  //   ALU
  //   Register B
  //   Internal Address Bus (4-Bits)
  //   Internal Data Bus
  //   MAR
  //   MBR
  //   Output Register
  //   External Adder Bus
  //   External Data Bus
endmodule

module Memory_Cell (
  input  Clock,
  input  WE,
  input  Din,
  input  OE,
  input  Reset,
  output Dout,
  output Stored_data
);

  wire and_1_out, and_2_out, not_1_out, or_1_out;

  not not_1 (not_1_out, WE);
  and and_1 (and_1_out, Stored_data, not_1_out);
  and and_2 (and_2_out, WE, Din);
  or or_1 (or_1_out, and_1_out, and_2_out);
  D_Flip_Flop d_ff_1 (.clk(Clock), .D(or_1_out), .Q(Stored_data), .reset(Reset));  // open: Qn, preset, en
  assign Dout = OE ? Stored_data : 1'bz;  // Controlled_Buffer controlled_buffer_1
endmodule

module Register (
  input  clock,
  input  WE,
  input  [7:0] Din,
  input  OE,
  output [7:0] Dout,
  output [7:0] Stored_data
);

  Memory_Cell _0 (
    .Clock(clock), .WE(WE), .Din(Din[0]), .OE(OE), .Dout(Dout[0]), .Stored_data(Stored_data[0]));  // open: Reset
  Memory_Cell _1 (
    .Clock(clock), .WE(WE), .Din(Din[1]), .OE(OE), .Dout(Dout[1]), .Stored_data(Stored_data[1]));  // open: Reset
  Memory_Cell _2 (
    .Clock(clock), .WE(WE), .Din(Din[2]), .OE(OE), .Dout(Dout[2]), .Stored_data(Stored_data[2]));  // open: Reset
  Memory_Cell _3 (
    .Clock(clock), .WE(WE), .Din(Din[3]), .OE(OE), .Dout(Dout[3]), .Stored_data(Stored_data[3]));  // open: Reset
  Memory_Cell _4 (
    .Clock(clock), .WE(WE), .Din(Din[4]), .OE(OE), .Dout(Dout[4]), .Stored_data(Stored_data[4]));  // open: Reset
  Memory_Cell _5 (
    .Clock(clock), .WE(WE), .Din(Din[5]), .OE(OE), .Dout(Dout[5]), .Stored_data(Stored_data[5]));  // open: Reset
  Memory_Cell _6 (
    .Clock(clock), .WE(WE), .Din(Din[6]), .OE(OE), .Dout(Dout[6]), .Stored_data(Stored_data[6]));  // open: Reset
  Memory_Cell _7 (
    .Clock(clock), .WE(WE), .Din(Din[7]), .OE(OE), .Dout(Dout[7]), .Stored_data(Stored_data[7]));  // open: Reset
endmodule

module ALU (
  input  [7:0] Reg_A,
  input  [7:0] Reg_B,
  input  OE,
  output [7:0] Dout,
  output [7:0] ALU_Result,
  output Carry_out
);

  Adder adder_1 (.a(Reg_A), .b(Reg_B), .out(ALU_Result), .cout(Carry_out));  // open: cin
  assign Dout = OE ? ALU_Result : 8'bz;  // Controlled_Buffer controlled_buffer_1

  // Notes on the sheet:
  //   ALU (8Bits)
endmodule

module MAR (
  input  clock,
  input  WE,
  input  [3:0] Din,
  input  OE,
  output [3:0] Dout,
  output [3:0] Stored_data
);

  Memory_Cell _0 (
    .Clock(clock), .WE(WE), .Din(Din[0]), .OE(OE), .Dout(Dout[0]), .Stored_data(Stored_data[0]));  // open: Reset
  Memory_Cell _1 (
    .Clock(clock), .WE(WE), .Din(Din[1]), .OE(OE), .Dout(Dout[1]), .Stored_data(Stored_data[1]));  // open: Reset
  Memory_Cell _2 (
    .Clock(clock), .WE(WE), .Din(Din[2]), .OE(OE), .Dout(Dout[2]), .Stored_data(Stored_data[2]));  // open: Reset
  Memory_Cell _3 (
    .Clock(clock), .WE(WE), .Din(Din[3]), .OE(OE), .Dout(Dout[3]), .Stored_data(Stored_data[3]));  // open: Reset
endmodule
